// Logisim project cla.circ as structural Verilog: 4 circuits, main circuit main
module main (
  input  Cin,
  input  A,
  input  B,
  output S,
  output P,
  output G,
  output Cout
);

  wire a_prime_b_prime_cin_out, a_prime_bcin_prime_out, ab_prime_cin_prime_out, abcin_out, acin_out, bcin_out;

  and abcin (abcin_out, A, B, Cin);
  and ab_prime_cin_prime (ab_prime_cin_prime_out, A, ~B, ~Cin);  // AND_Gate
  and a_prime_bcin_prime (a_prime_bcin_prime_out, ~A, B, ~Cin);  // AND_Gate
  and a_prime_b_prime_cin (a_prime_b_prime_cin_out, ~A, ~B, Cin);  // AND_Gate
  and acin (acin_out, A, Cin);
  and bcin (bcin_out, B, Cin);
  and ab (G, A, B);
  or a_b (P, A, B);
  or S_calc (S, abcin_out, ab_prime_cin_prime_out, a_prime_bcin_prime_out, a_prime_b_prime_cin_out);
  or cout_calc (Cout, acin_out, bcin_out, G);
endmodule

module CLA_PG1 (
  input  Cin,
  input  A,
  input  B,
  output S,
  output P,
  output G,
  output Cout
);

  wire a_prime_b_prime_cin_out, a_prime_bcin_prime_out, ab_prime_cin_prime_out, abcin_out, acin_out, bcin_out;

  and abcin (abcin_out, A, B, Cin);
  and ab_prime_cin_prime (ab_prime_cin_prime_out, A, ~B, ~Cin);  // AND_Gate
  and a_prime_bcin_prime (a_prime_bcin_prime_out, ~A, B, ~Cin);  // AND_Gate
  and a_prime_b_prime_cin (a_prime_b_prime_cin_out, ~A, ~B, Cin);  // AND_Gate
  and acin (acin_out, A, Cin);
  and bcin (bcin_out, B, Cin);
  and ab (G, A, B);
  or a_b (P, A, B);
  or S_calc (S, abcin_out, ab_prime_cin_prime_out, a_prime_bcin_prime_out, a_prime_b_prime_cin_out);
  or cout_calc (Cout, acin_out, bcin_out, G);
endmodule

module CL_BLOCK (
  input  Cin,
  input  Pin0,
  input  Gin0,
  input  Pin1,
  input  Gin1,
  input  Pin2,
  input  Gin2,
  output C0,
  output C1,
  output C2_Cout,
  output Pout,
  output Gout
);

  wire p0c0_out, p1g0_out, p1p0c0_out, p2g1_out, p2p1g0_out;

  and p0c0 (p0c0_out, Pin0, Cin);
  and p1p0c0 (p1p0c0_out, Pin1, Pin0, Cin);
  and p1g0 (p1g0_out, Pin1, Gin0);
  and p2p1p0 (Pout, Pin0, Pin1, Pin2);
  and p2p1g0 (p2p1g0_out, Pin1, Pin2, Gin0);
  and p2g1 (p2g1_out, Pin2, Gin1);
  or g0_p0c0 (C1, p0c0_out, Gin0);
  or g1_p1g0_p1p0c0 (C2_Cout, p1p0c0_out, Gin1, p1g0_out);
  or g2_p2g1_p2p1g0 (Gout, p2p1g0_out, Gin2, p2g1_out);

  assign C0 = Cin;
endmodule

module CLA_PG3 (
  input  Cin,
  input  [2:0] In1,
  input  [2:0] In2,
  output out_4,
  output out_5,
  output out_6,
  output P,
  output G,
  output Cout
);

  wire cl_block_1_c0, cl_block_1_c1, cla_pg1_1_g, cla_pg1_1_p, cla_pg1_2_g, cla_pg1_2_p, cla_pg1_3_g,
       cla_pg1_3_p;

  CLA_PG1 cla_pg1_1 (.A(In1[0]), .B(In2[0]), .Cin(Cin), .S(out_4), .P(cla_pg1_1_p), .G(cla_pg1_1_g));  // open: Cout
  CLA_PG1 cla_pg1_2 (
    .A(In1[1]), .B(In2[1]), .Cin(cl_block_1_c0), .S(out_5), .P(cla_pg1_2_p), .G(cla_pg1_2_g));  // open: Cout
  CLA_PG1 cla_pg1_3 (
    .A(In1[2]), .B(In2[2]), .Cin(cl_block_1_c1), .S(out_6), .P(cla_pg1_3_p), .G(cla_pg1_3_g));  // open: Cout
  CL_BLOCK cl_block_1 (
    .Pin0(cla_pg1_1_p), .Gin0(cla_pg1_1_g), .Pin1(cla_pg1_2_p), .Gin1(cla_pg1_2_g), .Pin2(cla_pg1_3_p),
    .Gin2(cla_pg1_3_g), .Cin(Cin), .C0(cl_block_1_c0), .C1(cl_block_1_c1), .C2_Cout(Cout), .Pout(P), .Gout(G));
endmodule
