// Logisim project Adder-32.circ as structural Verilog: 1 circuit, main circuit Adder-32
module Adder_32 (
  input  [31:0] A,
  input  [31:0] B,
  output [31:0] Result
);

  alu_32bit_mips alu_32bit_mips_1 (
    .B(B), .Ainvert(1'b0), .Bnegate(1'b0), .Oper(2'b10), .A(A), .Result(Result));  // open: CarryOut, Equal_Zero, Overflow
endmodule
