// Logisim project Instruction-Memory.circ as structural Verilog: 1 circuit, main circuit Instruction-Memory
module Instruction_Memory (
  input  [31:0] ReadAddress,
  output [31:0] Instruction
);

  ROM #(.addrWidth(6), .dataWidth(32)) rom_1 (.addr(ReadAddress[7:2]), .data(Instruction));  // open: sel
endmodule
